# Fritzing sketch Sketch (saved by Fritzing 0.9.3b)

parts:
  Part1 = Arduino Mega 2560 (Rev3)
  J1 = Basic Servo
  Power_plug1 = Power plug
  LED1 = LED - 5mm [color="Green (555nm)" package="5 mm [THT]"]
  R1 = Resistor [tolerance=±5% resistance=220 package=THT]

nets:
  GND: Part1.GND, J1.gnd, Power_plug1.GND, LED1.cathode
  N1: Part1.D11_PWM, R1.Pin_1
  N2: Part1.D9_PWM, J1.pulse
  VCC: J1.vcc, Power_plug1.VCC
  N3: LED1.anode, R1.Pin_0
